// Logisim project Lab02.circ as structural Verilog: 1 circuit, main circuit main
module main (
  input  A,
  input  B,
  input  C,
  output S0,
  output S1,
  output S2,
  output S3,
  output S4,
  output S5,
  output S6
);

  wire AB_out, ABC_out, AC_out, AnBC_out, AnBnC_out, AnC_out, BC_out, BnC_out, g1_out, nABC_out, nABnC_out,
       nAnB_out, nAnBC_out, nAnC_out, nBC_out, nBnC_out, not_1_out, not_2_out, not_3_out, or_1_out, or_3_out,
       or_6_out, or_8_out;

  not not_1 (not_1_out, A);
  and nBnC (nBnC_out, not_2_out, not_3_out);
  not not_2 (not_2_out, B);
  not not_3 (not_3_out, C);
  and BC (BC_out, B, C);
  and AnBnC (AnBnC_out, A, nBnC_out);
  and BnC (BnC_out, B, not_3_out);
  and AnC (AnC_out, not_3_out, A);
  and AC (AC_out, C, A);
  and nAnB (nAnB_out, not_1_out, not_2_out);
  and nABnC (nABnC_out, not_1_out, BnC_out);
  and nABC (nABC_out, not_1_out, BC_out);
  and nBC (nBC_out, not_2_out, C);
  and AB (AB_out, A, B);
  and ABC (ABC_out, AC_out, B);
  or g1 (g1_out, AC_out, nABnC_out);
  and nAnBC (nAnBC_out, nAnB_out, C);
  or or_1 (or_1_out, nAnB_out, nBnC_out);
  or or_2 (S3, nABC_out, AnC_out);
  or or_3 (or_3_out, AnBnC_out, ABC_out);
  not not_4 (S0, g1_out);
  or or_4 (S2, ABC_out, or_1_out);
  and AnBC (AnBC_out, A, nBC_out);
  not not_5 (S4, AnBC_out);
  or or_5 (S1, or_3_out, nAnBC_out);
  or or_6 (or_6_out, nAnBC_out, BnC_out);
  or or_7 (S6, or_6_out, AB_out);
  and nAnC (nAnC_out, not_3_out, not_1_out);
  or or_8 (or_8_out, nAnC_out, AnBC_out);
  not not_6 (S5, or_8_out);
  _7_Segment_Display L_7_Segment_Display_1 (.g(S6), .f(S5), .a(S0), .b(S1), .e(S4), .d(S3), .c(S2));  // open: dp
endmodule
