// Logisim project mux1to2.circ as structural Verilog: 2 circuits, main circuit main
module main (
  input  s2,
  input  s1,
  input  input1,
  input  s3,
  output output1,
  output output2,
  output output3,
  output output4,
  output output5,
  output output6
);

  wire d1_x, d1_y, d2_x, d2_y;

  DEMUX d1 (.m(input1), .s(s3), .x(d1_x), .y(d1_y));
  DEMUX d2 (.m(d1_x), .s(s2), .x(d2_x), .y(d2_y));
  DEMUX d3 (.m(d2_x), .s(s1), .x(output1), .y(output2));
  DEMUX d4 (.m(d2_y), .s(s1), .x(output3), .y(output4));
  DEMUX d5 (.m(d1_y), .s(s1), .x(output5), .y(output6));
endmodule

module DEMUX (
  input  m,
  input  s,
  output x,
  output y
);

  wire not_1_out;

  not not_1 (not_1_out, s);
  and and_1 (x, m, not_1_out);
  and and_2 (y, s, m);
endmodule
