// Logisim project mux1to6.circ as structural Verilog: 1 circuit, main circuit main
module main (
  input  input1,
  input  s2,
  input  s1,
  input  s3,
  output out_5,
  output out_6,
  output out_7,
  output out_8,
  output out_9,
  output out_10
);

  wire demultiplexer_1_out0, demultiplexer_1_out1, demultiplexer_2_out0, demultiplexer_2_out1;

  Demultiplexer #(.enable("false")) demultiplexer_1 (
    .out0(demultiplexer_1_out0), .out1(demultiplexer_1_out1), .in(input1), .sel(s3));
  Demultiplexer #(.enable("false")) demultiplexer_2 (
    .out0(demultiplexer_2_out0), .out1(demultiplexer_2_out1), .in(demultiplexer_1_out0), .sel(s2));
  Demultiplexer #(.enable("false")) demultiplexer_3 (.out0(out_5), .out1(out_6), .in(demultiplexer_2_out0), .sel(s1));
  Demultiplexer #(.enable("false")) demultiplexer_4 (.out0(out_7), .out1(out_8), .in(demultiplexer_2_out1), .sel(s1));
  Demultiplexer #(.enable("false")) demultiplexer_5 (.out0(out_9), .out1(out_10), .in(demultiplexer_1_out1), .sel(s1));
endmodule
