// Logisim project mux6to1.circ as structural Verilog: 2 circuits, main circuit main
module main (
  input  A,
  input  B,
  input  S2,
  input  S1,
  input  C,
  input  S3,
  input  D,
  input  E,
  input  F,
  output OUTPUT1
);

  wire L1_output1, L2_output1, L3_output1, L4_output1;

  c1 L1 (.input1(A), .S1(S3), .input2(B), .output1(L1_output1));
  c1 L2 (.input1(C), .S1(S3), .input2(D), .output1(L2_output1));
  c1 L3 (.input1(E), .S1(S3), .input2(F), .output1(L3_output1));
  c1 L4 (.input1(L1_output1), .S1(S2), .input2(L2_output1), .output1(L4_output1));
  c1 L5 (.input1(L4_output1), .S1(S1), .input2(L3_output1), .output1(OUTPUT1));
endmodule

module c1 (
  input  input1,
  input  S1,
  input  input2,
  output output1
);

  wire and_1_out, and_2_out, not_1_out;

  not not_1 (not_1_out, S1);
  and and_1 (and_1_out, input1, not_1_out);
  and and_2 (and_2_out, S1, input2);
  or or_1 (output1, and_1_out, and_2_out);
endmodule
