// Logisim project DLatches.circ as structural Verilog: 1 circuit, main circuit main
module main (
  input  S,
  input  C,
  output notQ,
  output Q
);

  wire and_1_out, and_2_out, not_1_out;

  not not_1 (not_1_out, S);
  and and_1 (and_1_out, S, C);
  and and_2 (and_2_out, C, not_1_out);
  nor nor_1 (notQ, and_1_out, Q);
  nor nor_2 (Q, notQ, and_2_out);
endmodule
