// Logisim project SRLatches.circ as structural Verilog: 1 circuit, main circuit main
module main (
  input  S,
  input  C,
  input  R,
  output notQ,
  output Q
);

  wire and_1_out, and_2_out;

  and and_1 (and_1_out, S, C);
  and and_2 (and_2_out, C, R);
  nor nor_1 (notQ, and_1_out, Q);
  nor nor_2 (Q, notQ, and_2_out);
endmodule
