// Logisim project pen.circ as structural Verilog: 3 circuits, main circuit pen
module main (
  input  D,
  input  C,
  output Q
);

  wire d1_q, not_1_out;

  not not_1 (not_1_out, C);
  DLATCHES d1 (.D(D), .C(not_1_out), .Q(d1_q));  // open: notQ
  DLATCHES d2 (.D(d1_q), .C(C), .Q(Q));  // open: notQ
endmodule

module DLATCHES (
  input  D,
  input  C,
  output notQ,
  output Q
);

  wire and_1_out, and_2_out, not_1_out;

  not not_1 (not_1_out, D);
  and and_1 (and_1_out, D, C);
  and and_2 (and_2_out, C, not_1_out);
  nor nor_1 (notQ, and_1_out, Q);
  nor nor_2 (Q, notQ, and_2_out);
endmodule

module pen (
  input  clock,
  input  reset
);

  wire and_1_out, and_2_out, and_3_out, and_4_out, and_5_out, and_6_out, and_7_out, and_8_out, and_9_out,
       and_10_out, and_11_out, and_12_out, F0_q, F0_qn, F1_q, F1_qn, F2_q, F2_qn, F3_q, F3_qn, or_1_out,
       or_2_out, or_3_out, or_4_out, or_5_out;

  or or_1 (or_1_out, and_4_out, and_1_out);
  or or_2 (or_2_out, and_7_out, and_5_out, and_2_out);
  D_Flip_Flop F3 (.D(or_1_out), .clk(clock), .Q(F3_q), .Qn(F3_qn), .reset(reset));  // open: preset
  and and_1 (and_1_out, F0_qn, F2_q, F3_q);
  and and_2 (and_2_out, F1_q, F2_q, F3_q);
  D_Flip_Flop F2 (.D(or_2_out), .clk(clock), .Q(F2_q), .Qn(F2_qn), .reset(reset));  // open: preset
  and and_3 (and_3_out, F3_q, F2_q, F0_qn);
  and and_4 (and_4_out, F0_qn, F1_qn);
  D_Flip_Flop F1 (.D(or_3_out), .clk(clock), .Q(F1_q), .Qn(F1_qn), .reset(reset));  // open: preset
  or or_3 (or_3_out, and_3_out, and_6_out);
  and and_5 (and_5_out, F3_qn, F1_qn, F0_q);
  and and_6 (and_6_out, F2_q, F1_q, F0_q);
  D_Flip_Flop F0 (.D(or_4_out), .clk(clock), .Q(F0_q), .Qn(F0_qn), .reset(reset));  // open: preset
  and and_7 (and_7_out, F3_q, F1_qn, F0_qn);
  and and_8 (and_8_out, F2_qn, F0_q, F3_qn);
  and and_9 (and_9_out, F0_q, F2_qn, F3_qn);
  and and_10 (and_10_out, F3_q, F1_q, F2_q);
  and and_11 (and_11_out, F0_q, F1_q, F2_q);
  and and_12 (and_12_out, F1_qn, F0_q, F2_q, F3_qn);
  or or_4 (or_4_out, and_9_out, and_10_out, and_11_out);
  or or_5 (or_5_out, and_8_out, and_12_out);
  LED light (.in(or_5_out));
endmodule
