// Logisim project pen2.circ as structural Verilog: 1 circuit, main circuit main
module main (
  input  in_1,
  input  in_2
);

  wire f0_qn, f0gate_out, f1_q, f1_qn, f1gate_out, f2_q, f2_qn, f2gate_out, f2nf1nf0_out, f3_q, f3_qn,
       f3f2nf1nf0_out, f3gate_out, nf3f1nf0_out, nf3f2f1_out, nf3f2f1nf0_out, nf3nf2_out, nf3nf2f1_out,
       nf3nf2nf1_out;

  or f0gate (f0gate_out, f3f2nf1nf0_out, nf3f2f1_out, nf3nf2nf1_out);
  and f3f2nf1nf0 (f3f2nf1nf0_out, f0_qn, f1_qn, f2_q, f3_q);
  and nf3f2f1 (nf3f2f1_out, f1_q, f2_q, f3_qn);
  and nf3nf2nf1 (nf3nf2nf1_out, f1_qn, f3_qn);
  D_Flip_Flop f3 (.D(f3gate_out), .clk(in_1), .Q(f3_q), .Qn(f3_qn), .reset(in_2));  // open: preset
  or f3gate (f3gate_out, f3f2nf1nf0_out, nf3f2f1nf0_out);
  D_Flip_Flop f2 (.D(f2gate_out), .clk(in_1), .Q(f2_q), .Qn(f2_qn), .reset(in_2));  // open: preset
  D_Flip_Flop f1 (.D(f1gate_out), .clk(in_1), .Q(f1_q), .Qn(f1_qn), .reset(in_2));  // open: preset
  D_Flip_Flop f0 (.D(f0gate_out), .clk(in_1), .Qn(f0_qn), .reset(in_2));  // open: Q, preset
  or f1gate (f1gate_out, nf3f1nf0_out, nf3nf2f1_out);
  and nf3f2f1nf0 (nf3f2f1nf0_out, f3_qn, f2_q, f1_q, f0_qn);
  and nf3f1nf0 (nf3f1nf0_out, f0_qn, f1_q, f3_qn);
  and nf3nf2f1 (nf3nf2f1_out, f1_q, f2_qn, f3_qn);
  or f2gate (f2gate_out, nf3f1nf0_out, f2nf1nf0_out, nf3nf2_out);
  and f2nf1nf0 (f2nf1nf0_out, f2_q, f1_qn, f0_qn);
  and nf3nf2 (nf3nf2_out, f2_qn, f3_qn);
endmodule
