// Logisim project pen3.circ as structural Verilog: 1 circuit, main circuit main
module main (
  input  in_1,
  input  in_2
);

  wire f0_q, f0_qn, f1_q, f1_qn, f2_q, f2_qn, f2f1f0_out, f3_q, f3_qn, f3f2f1_out, f3f2f1nf0_out,
       f3f2nf0_out, f3nf1f0_out, f3nf1nf0_out, nf3nf1f0_out, nf3nf2f0_out, nf3nf2nf1nf0_out, or_1_out,
       or_2_out, or_3_out, or_4_out;

  or or_1 (or_1_out, f3f2f1_out, f2f1f0_out, nf3nf2f0_out);
  and f3f2f1nf0 (f3f2f1nf0_out, f3f2f1_out, f0_qn);
  and f3f2f1 (f3f2f1_out, f1_q, f2_q, f3_q);
  and f2f1f0 (f2f1f0_out, f0_q, f1_q, f2_q);
  and nf3nf2f0 (nf3nf2f0_out, f0_q, f2_qn, f3_qn);
  D_Flip_Flop f3 (.D(or_4_out), .clk(in_1), .Q(f3_q), .Qn(f3_qn), .reset(in_2));  // open: preset
  D_Flip_Flop f2 (.D(or_3_out), .clk(in_1), .Q(f2_q), .Qn(f2_qn), .reset(in_2));  // open: preset
  D_Flip_Flop f1 (.D(or_2_out), .clk(in_1), .Q(f1_q), .Qn(f1_qn), .reset(in_2));  // open: preset
  D_Flip_Flop f0 (.D(or_1_out), .clk(in_1), .Q(f0_q), .Qn(f0_qn), .reset(in_2));  // open: preset
  or or_2 (or_2_out, f2f1f0_out, f3f2nf0_out);
  and nf3nf2nf1nf0 (nf3nf2nf1nf0_out, f3_qn, in_1, f1_qn, f0_qn);
  and f3nf1nf0 (f3nf1nf0_out, f3_q, f1_qn, f0_qn);
  and f3f2nf0 (f3f2nf0_out, f0_qn, f2_q, f3_q);
  or or_3 (or_3_out, f3f2f1_out, f3nf1f0_out, nf3nf1f0_out);
  or or_4 (or_4_out, nf3nf2nf1nf0_out, f3nf1nf0_out, f3f2f1nf0_out);
  and f3nf1f0 (f3nf1f0_out, f0_q, f3_q);
  and nf3nf1f0 (nf3nf1f0_out, f0_q, f1_qn, f3_qn);
endmodule
