// Logisim project Lab06.circ as structural Verilog: 1 circuit, main circuit main
module main (
  input  clock,
  input  Enable,
  input  [1:0] Wregister,
  input  [1:0] Rregister,
  input  [3:0] WriteData,
  output [3:0] u
);

  wire demultiplexer_1_out0, demultiplexer_1_out1, demultiplexer_1_out2, demultiplexer_1_out3;
  wire [3:0] r1_q, r2_q, r3_q, r4_q;

  Demultiplexer #(.select(2), .enable("false")) demultiplexer_1 (
    .out0(demultiplexer_1_out0), .out1(demultiplexer_1_out1), .out2(demultiplexer_1_out2),
    .out3(demultiplexer_1_out3), .in(Enable), .sel(Wregister));
  Register #(.width(4)) r1 (.D(WriteData), .en(demultiplexer_1_out0), .clk(clock), .Q(r1_q));  // open: clr
  Register #(.width(4)) r2 (.D(WriteData), .en(demultiplexer_1_out1), .clk(clock), .Q(r2_q));  // open: clr
  Register #(.width(4)) r3 (.D(WriteData), .en(demultiplexer_1_out2), .clk(clock), .Q(r3_q));  // open: clr
  Register #(.width(4)) r4 (.D(WriteData), .en(demultiplexer_1_out3), .clk(clock), .Q(r4_q));  // open: clr
  Multiplexer #(.select(2), .width(4)) multiplexer_1 (
    .in0(r1_q), .in1(r2_q), .in2(r3_q), .in3(r4_q), .out(u), .sel(Rregister));  // open: en
endmodule
